// Logisim project laboratorio.circ as structural Verilog: 1 circuit, main circuit main
module main (
  input  in_1,
  input  in_2,
  input  in_3,
  input  in_4
);

  wire and_1_out, and_2_out, and_3_out, and_4_out, and_5_out, and_6_out, and_7_out, and_8_out, and_9_out,
       and_10_out, and_11_out, and_12_out, and_13_out, and_14_out, and_15_out, not_1_out, not_2_out,
       not_3_out, not_4_out, or_1_out, or_3_out, or_4_out, or_5_out, or_6_out;

  not not_1 (not_1_out, in_1);
  not not_2 (not_2_out, in_2);
  not not_3 (not_3_out, in_3);
  not not_4 (not_4_out, in_4);
  and and_1 (and_1_out, in_2, in_4);
  and and_2 (and_2_out, not_2_out, in_3);
  and and_3 (and_3_out, not_2_out, not_4_out);
  and and_4 (and_4_out, in_2, in_3);
  and and_5 (and_5_out, not_1_out, in_4);
  and and_6 (and_6_out, in_4, not_2_out);
  and and_7 (and_7_out, not_3_out, not_2_out);
  and and_8 (and_8_out, in_1, not_3_out, not_4_out);
  and and_9 (and_9_out, in_3, in_4);
  and and_10 (and_10_out, not_2_out, not_3_out);
  and and_11 (and_11_out, in_1, in_2, not_4_out);
  and and_12 (and_12_out, in_1, in_4);
  and and_13 (and_13_out, in_1, not_3_out);
  and and_14 (and_14_out, in_4, not_3_out);
  and and_15 (and_15_out, in_3, not_1_out, not_4_out);
  or or_1 (or_1_out, in_3, in_4, not_1_out, not_2_out);
  // OR_Gate or_2 is placed but not wired
  // AND_Gate and_16 is placed but not wired
  // AND_Gate and_17 is placed but not wired
  // AND_Gate and_18 is placed but not wired
  or or_3 (or_3_out, not_1_out, and_1_out, and_2_out, and_3_out);
  or or_4 (or_4_out, and_4_out, and_5_out, and_6_out, and_7_out, and_8_out);
  or or_5 (or_5_out, and_9_out, and_10_out, and_11_out);
  or or_6 (or_6_out, in_2, and_12_out, and_13_out, and_14_out, and_15_out);
  _7_Segment_Display u_7_segment_display_1 (
    .f(or_1_out), .a(or_3_out), .b(or_4_out), .d(or_6_out), .c(or_5_out));  // open: g, e, dp
endmodule
